# Fritzing sketch TicTacToeMachine (saved by Fritzing 0.8.0b)
breadboards: 4

parts:
  R_in_3 = Resistor [tolerance=±5% resistance=10k package=THT]
  R_in_2 = Resistor [tolerance=±5% resistance=10k package=THT]
  R_in_1 = Resistor [tolerance=±5% resistance=10k package=THT]
  CMOS_AND1 = mystery part, 14 pins [chip_label="CMOS4073 (3AND)"]
  VCC1 = 4 x AAA Battery Mount
  R1R = Resistor [tolerance=±5% resistance=100 package=THT]
  R2R = Resistor [tolerance=±5% resistance=100 package=THT]
  R3R = Resistor [tolerance=±5% resistance=100 package=THT]
  CMOS_OR1 = mystery part, 14 pins [chip_label=4OR]
  R_OR1_in1 = Resistor [tolerance=±5% resistance=10k package=THT]
  R_OR1_in2 = Resistor [tolerance=±5% resistance=10k package=THT]
  LED4_R = LED - 5mm [color="Red (633nm)" package="5 mm [THT]"]
  LED5_R = LED - 5mm [color="Red (633nm)" package="5 mm [THT]"]
  LED6_R = LED - 5mm [color="Red (633nm)" package="5 mm [THT]"]
  LED7_R = LED - 5mm [color="Red (633nm)" package="5 mm [THT]"]
  LED8_R = LED - 5mm [color="Red (633nm)" package="5 mm [THT]"]
  LED9_R = LED - 5mm [color="Red (633nm)" package="5 mm [THT]"]
  R6R = Resistor [tolerance=±5% resistance=100 package=THT]
  R5R = Resistor [tolerance=±5% resistance=100 package=THT]
  R4R = Resistor [tolerance=±5% resistance=100 package=THT]
  R9R = Resistor [tolerance=±5% resistance=100 package=THT]
  R7R = Resistor [tolerance=±5% resistance=100 package=THT]
  R8R = Resistor [tolerance=±5% resistance=100 package=THT]
  Led_HR2_R = LED - 5mm [color="Infrared (940nm)" package="5 mm [THT]"]
  Led_HR3_R = LED - 5mm [color="Infrared (940nm)" package="5 mm [THT]"]
  R_HR3_R = Resistor [tolerance=±5% resistance=100 package=THT]
  J1 = male pin header, 4 pins [form="♂ (male)"]
  J2 = male pin header, 4 pins [form="♂ (male)"]
  J3 = male pin header, 4 pins [form="♂ (male)"]
  J4 = male pin header, 4 pins [form="♂ (male)"]
  J5 = male pin header, 4 pins [form="♂ (male)"]
  J6 = male pin header, 4 pins [form="♂ (male)"]
  J7 = male pin header, 4 pins [form="♂ (male)"]
  J8 = male pin header, 4 pins [form="♂ (male)"]
  J9 = male pin header, 4 pins [form="♂ (male)"]
  LED1_R = LED - 5mm [color="Red (633nm)" package="5 mm [THT]"]
  LED2_R = LED - 5mm [color="Red (633nm)" package="5 mm [THT]"]
  LED3_R = LED - 5mm [color="Red (633nm)" package="5 mm [THT]"]
  R_HR2_R = Resistor [tolerance=±5% resistance=100 package=THT]
  R_HR1_R1 = Resistor [tolerance=±5% resistance=100 package=THT]
  Led_HR1_R1 = LED - 5mm [color="Infrared (940nm)" package="5 mm [THT]"]
  LED7_G = LED - 5mm [color="Green (555nm)" package="5 mm [THT]"]
  LED4_G = LED - 5mm [color="Green (555nm)" package="5 mm [THT]"]
  LED1_G = LED - 5mm [color="Green (555nm)" package="5 mm [THT]"]
  LED8_G = LED - 5mm [color="Green (555nm)" package="5 mm [THT]"]
  LED5_G = LED - 5mm [color="Green (555nm)" package="5 mm [THT]"]
  LED2_G = LED - 5mm [color="Green (555nm)" package="5 mm [THT]"]
  LED9_G = LED - 5mm [color="Green (555nm)" package="5 mm [THT]"]
  LED6_G = LED - 5mm [color="Green (555nm)" package="5 mm [THT]"]
  LED3_G = LED - 5mm [color="Green (555nm)" package="5 mm [THT]"]
  R8_G = Resistor [tolerance=±5% resistance=100 package=THT]
  R9_G = Resistor [tolerance=±5% resistance=100 package=THT]
  R6_G = Resistor [tolerance=±5% resistance=100 package=THT]
  R3_G = Resistor [tolerance=±5% resistance=100 package=THT]
  R5_G = Resistor [tolerance=±5% resistance=100 package=THT]
  R2_G = Resistor [tolerance=±5% resistance=100 package=THT]
  R7_G = Resistor [tolerance=±5% resistance=100 package=THT]
  R4_G = Resistor [tolerance=±5% resistance=100 package=THT]
  R1_G = Resistor [tolerance=±5% resistance=100 package=THT]
  Led_Win_R = LED - 5mm [color="Red (633nm)" package="5 mm [THT]"]
  R_WIN_R = Resistor [tolerance=±5% resistance=100 package=THT]

nets:
  N1: R_in_3.Pin_0, R_in_2.Pin_0, R_in_1.Pin_0, CMOS_AND1.pin7, VCC1.-, R1R.Pin_1, R2R.Pin_1, R3R.Pin_1, CMOS_OR1.pin7, R_OR1_in1.Pin_0, R_OR1_in2.Pin_0, R6R.Pin_1, R5R.Pin_1, R4R.Pin_1, R9R.Pin_1, R7R.Pin_1, R8R.Pin_1, R_HR3_R.Pin_1, R_HR2_R.Pin_1, R_HR1_R1.Pin_1, R8_G.Pin_1, R9_G.Pin_1, R6_G.Pin_1, R3_G.Pin_1, R5_G.Pin_1, R2_G.Pin_1, R7_G.Pin_1, R4_G.Pin_1, R1_G.Pin_1, R_WIN_R.Pin_1
  N2: R_in_3.Pin_1, CMOS_AND1.pin5, J3.pin1, LED3_R.anode
  N3: R_in_2.Pin_1, CMOS_AND1.pin4, J2.pin1, LED2_R.anode
  N4: R_in_1.Pin_1, CMOS_AND1.pin3, J1.pin1, LED1_R.anode
  N5: CMOS_AND1.pin6, CMOS_OR1.pin1, Led_HR1_R1.anode
  N6: VCC1.+, CMOS_OR1.pin14, J1.pin4, J2.pin4, J3.pin4, J4.pin4, J5.pin4, J6.pin4, J7.pin4, J8.pin4, J9.pin4
  N7: R1R.Pin_0, LED1_R.cathode
  N8: R2R.Pin_0, LED2_R.cathode
  N9: R3R.Pin_0, LED3_R.cathode
  N10: CMOS_OR1.pin3, Led_Win_R.anode
  N11: LED4_R.cathode, R4R.Pin_0
  N12: LED4_R.anode, J4.pin1
  N13: LED5_R.cathode, R5R.Pin_0
  N14: LED5_R.anode, J5.pin1
  N15: LED6_R.cathode, R6R.Pin_0
  N16: LED6_R.anode, J6.pin1
  N17: LED7_R.cathode, R7R.Pin_0
  N18: LED7_R.anode, J7.pin1
  N19: LED8_R.cathode, R8R.Pin_0
  N20: LED8_R.anode, J8.pin1
  N21: LED9_R.cathode, R9R.Pin_0
  N22: LED9_R.anode, J9.pin1
  N23: Led_HR2_R.cathode, R_HR2_R.Pin_0
  N24: Led_HR3_R.cathode, R_HR3_R.Pin_0
  N25: J1.pin3, LED1_G.anode
  N26: J2.pin3, LED2_G.anode
  N27: J3.pin3, LED3_G.anode
  N28: J4.pin3, LED4_G.anode
  N29: J5.pin3, LED5_G.anode
  N30: J6.pin3, LED6_G.anode
  N31: J7.pin3, LED7_G.anode
  N32: J8.pin3, LED8_G.anode
  N33: J9.pin3, LED9_G.anode
  N34: R_HR1_R1.Pin_0, Led_HR1_R1.cathode
  N35: LED7_G.cathode, R7_G.Pin_0
  N36: LED4_G.cathode, R4_G.Pin_0
  N37: LED1_G.cathode, R1_G.Pin_0
  N38: LED8_G.cathode, R8_G.Pin_0
  N39: LED5_G.cathode, R5_G.Pin_0
  N40: LED2_G.cathode, R2_G.Pin_0
  N41: LED9_G.cathode, R9_G.Pin_0
  N42: LED6_G.cathode, R6_G.Pin_0
  N43: LED3_G.cathode, R3_G.Pin_0
  N44: Led_Win_R.cathode, R_WIN_R.Pin_0

notes:
  These LED indicates that player red has gotten three in a row on the horizontal rows
  This section handles
  1) The power for each individual arena LED's
  2) passes the arena's state to the next
  This section handles:
  1) Detection if a player has gotten three in a row
  2) If yes, passes it to the next section
  This LED indicates that player red has three in a row
  This section handles the display of a player having three in a row
  Each connection from below goes to two or three 3AND ports in the section below
  Per player there will be 8 connection from the upper section the the lower section
  1: pin 1 of rotary switch, Red player active
  2: pin 2 of rotary switch, no player active
  3: pin 3 of rotary switch, Green player active
  4: pin A of rotary switch
  These headers are connected to the rotary switches.
  Order:
  top-left, top-mid, top-right,
  mid-left, mid-mid, right-mid,
  bottom-left, bottom-mid, bottom-right
